# Fritzing sketch schematic (saved by Fritzing 0.9.3b)
circuit board: 8.46667cm x 5.64444cm
breadboards: 1

parts:
  USB-C_Nano = Arduino Nano (Rev3.0) (ICSP)
  J1 = Basic Servo
  J2 = Basic Servo
  J3 = Basic Servo
  J4 = Basic Servo
  USB-C_ESP32 = LuaNode32 / ESP32 [part_number=ESP32S-PIN30]
  Power_plug_9v = Power plug

nets:
  GND: USB-C_Nano.GND, J1.gnd, J2.gnd, J3.gnd, J4.gnd, USB-C_ESP32.GND, Power_plug_9v.GND
  N1: USB-C_Nano.D2, USB-C_ESP32.D12
  N2: USB-C_Nano.D3, USB-C_ESP32.D14
  N3: USB-C_Nano.D4, USB-C_ESP32.D27
  N4: USB-C_Nano.D5, USB-C_ESP32.D26
  N5: USB-C_Nano.D6, J4.pulse
  N6: USB-C_Nano.D7, J3.pulse
  N7: USB-C_Nano.D8, J2.pulse
  N8: USB-C_Nano.D9, J1.pulse
  VIN: USB-C_Nano.VIN, USB-C_ESP32.Vin, Power_plug_9v.VCC
  VCC: USB-C_Nano.5V, J1.vcc, J2.vcc, J3.vcc, J4.vcc

custom parts:
  LuaNode32 / ESP32: New Image for LuaNode32 DOIT ESP32 DEVKIT V1. Base parts from LuaNode32 / ESP32 ESP32 based LuaNode32 by G.Noorlander DOIT Esp32 DevKit v1 (30 pins long, 11 pins width) by Werner Rothschopf (modified by vanepp Dec 2018)
